# Fritzing sketch diag (saved by Fritzing 0.9.3b)
breadboards: 1

parts:
  Part1 = Arduino Uno (Rev3)
  R1 = Resistor [tolerance=±5% resistance=220 package=THT]
  R2 = Resistor [tolerance=±5% resistance=220 package=THT]
  R3 = Resistor [tolerance=±5% resistance=220 package=THT]
  R4 = Resistor [tolerance=±5% resistance=220 package=THT]
  R5 = Resistor [tolerance=±5% resistance=220 package=THT]
  R6 = Resistor [tolerance=±5% resistance=220 package=THT]
  LED1 = LED - 5mm [color="Red (633nm)" package="5 mm [THT]"]
  LED2 = LED - 5mm [color="Red (633nm)" package="5 mm [THT]"]
  LED3 = LED - 5mm [color="Red (633nm)" package="5 mm [THT]"]
  LED4 = LED - 5mm [color="Red (633nm)" package="5 mm [THT]"]
  LED5 = LED - 5mm [color="Red (633nm)" package="5 mm [THT]"]
  LED6 = LED - 5mm [color="Red (633nm)" package="5 mm [THT]"]

nets:
  N1: Part1.D8, R6.Pin_0
  N2: Part1.D9_PWM, R5.Pin_0
  N3: Part1.D10_PWM/SS, R4.Pin_0
  N4: Part1.D11_PWM/MOSI, R3.Pin_0
  N5: Part1.D12/MISO, R2.Pin_0
  N6: Part1.D13/SCK, R1.Pin_0
  N7: Part1.GND, LED1.cathode, LED2.cathode, LED3.cathode, LED4.cathode, LED5.cathode, LED6.cathode
  N8: R1.Pin_1, LED6.anode
  N9: R2.Pin_1, LED5.anode
  N10: R3.Pin_1, LED4.anode
  N11: R4.Pin_1, LED3.anode
  N12: R5.Pin_1, LED2.anode
  N13: R6.Pin_1, LED1.anode

notes:
  Martin Miksik
