# Fritzing sketch 6diagram (saved by Fritzing 0.9.3b)
breadboards: 1

parts:
  Part1 = Arduino Uno (Rev3) - ICSP
  S1 = Momentary Switch [package=ksa_sealed_tac_switch]
  S2 = Momentary Switch [package=ksa_sealed_tac_switch]
  LED1 = smd LED [color="Red (633nm)" package="0805 [SMD]"]
  LED2 = smd LED [color="Green (555nm)" package="0805 [SMD]"]
  LED3 = smd LED [color="Blue (470nm)" package="0805 [SMD]"]
  R1 = Resistor [tolerance=±5% resistance=220 package="0805 [SMD]"]
  R2 = Resistor [tolerance=±5% resistance=220 package="0805 [SMD]"]
  R3 = Resistor [tolerance=±5% resistance=220 package="0805 [SMD]"]
  R4 = Photocell (LDR) [package=THT]
  R5 = Resistor [tolerance=±5% resistance=1k package="0805 [SMD]"]

nets:
  N1: Part1.A0, Part1.5V, R4.pin_0, R4.pin_1, R5.Pin_0
  N2: Part1.GND, S1.2, S2.2, LED1.cathode, LED2.cathode, LED3.cathode, R5.Pin_1
  N3: Part1.D2, S2.4
  N4: Part1.D3_PWM, R3.Pin_0
  N5: Part1.D5_PWM, R1.Pin_0
  N6: Part1.D6_PWM, R2.Pin_0
  N7: Part1.D7, S1.4
  N8: LED1.anode, R1.Pin_1
  N9: LED2.anode, R2.Pin_1
  N10: LED3.anode, R3.Pin_1
